// Logisim project 8 bit d flip flop.circ as structural Verilog: 1 circuit, main circuit main
module main (
  input  CLK,
  input  EN,
  input  CLR,
  input  [7:0] D,
  output [7:0] Q
);

  D_Flip_Flop d_ff_1 (.clk(CLK), .D(D[0]), .Q(Q[0]), .en(EN), .reset(CLR));  // open: Qn, preset
  D_Flip_Flop d_ff_2 (.clk(CLK), .D(D[1]), .Q(Q[1]), .en(EN), .reset(CLR));  // open: Qn, preset
  D_Flip_Flop d_ff_3 (.clk(CLK), .D(D[2]), .Q(Q[2]), .en(EN), .reset(CLR));  // open: Qn, preset
  D_Flip_Flop d_ff_4 (.clk(CLK), .D(D[3]), .Q(Q[3]), .en(EN), .reset(CLR));  // open: Qn, preset
  D_Flip_Flop d_ff_5 (.clk(CLK), .D(D[4]), .Q(Q[4]), .en(EN), .reset(CLR));  // open: Qn, preset
  D_Flip_Flop d_ff_6 (.clk(CLK), .D(D[5]), .Q(Q[5]), .en(EN), .reset(CLR));  // open: Qn, preset
  D_Flip_Flop d_ff_7 (.clk(CLK), .D(D[6]), .Q(Q[6]), .en(EN), .reset(CLR));  // open: Qn, preset
  D_Flip_Flop d_ff_8 (.clk(CLK), .D(D[7]), .Q(Q[7]), .en(EN), .reset(CLR));  // open: Qn, preset
endmodule
