// Logisim project Part 2a.circ as structural Verilog: 1 circuit, main circuit main
module main (
  input  [3:0] RegSel,
  input  [2:0] OutASel,
  input  [1:0] FunSel,
  input  CLK,
  input  [7:0] I,
  input  [2:0] OutBSel,
  input  [3:0] TmpSel,
  output [7:0] OutA,
  output [7:0] OutB
);

  wire undriven, undriven_2, undriven_3, undriven_4, undriven_5, undriven_6;
  wire [3:0] not_1_out, not_2_out;
  wire [7:0] R1_output, R2_output, R3_output, R4_output, T1_output, T2_output, T3_output, T4_output;

  Hex_Digit_Display hex_digit_display_1 (.value(RegSel));  // open: dp
  Hex_Digit_Display hex_digit_display_2 (.value(I[7:4]), .dp(undriven));
  Hex_Digit_Display hex_digit_display_3 (.value(I[3:0]), .dp(undriven_2));
  Hex_Digit_Display hex_digit_display_4 (.value(TmpSel));  // open: dp
  assign not_1_out = ~TmpSel;  // NOT_Gate not_1, 4 bits wide
  assign not_2_out = ~RegSel;  // NOT_Gate not_2, 4 bits wide
  _8_bit_reg_main R1 (.Input(I), .FunSel(FunSel), .Enable(not_2_out[3]), .CLK(CLK), .Output(R1_output));
  _8_bit_reg_main R2 (.Input(I), .FunSel(FunSel), .Enable(not_2_out[2]), .CLK(CLK), .Output(R2_output));
  _8_bit_reg_main R3 (.Input(I), .FunSel(FunSel), .Enable(not_2_out[1]), .CLK(CLK), .Output(R3_output));
  _8_bit_reg_main R4 (.Input(I), .FunSel(FunSel), .Enable(not_2_out[0]), .CLK(CLK), .Output(R4_output));
  _8_bit_reg_main T1 (.Input(I), .FunSel(FunSel), .Enable(not_1_out[3]), .CLK(CLK), .Output(T1_output));
  _8_bit_reg_main T2 (.Input(I), .FunSel(FunSel), .Enable(not_1_out[2]), .CLK(CLK), .Output(T2_output));
  _8_bit_reg_main T3 (.Input(I), .FunSel(FunSel), .Enable(not_1_out[1]), .CLK(CLK), .Output(T3_output));
  _8_bit_reg_main T4 (.Input(I), .FunSel(FunSel), .Enable(not_1_out[0]), .CLK(CLK), .Output(T4_output));
  Multiplexer #(.select(3), .width(8), .enable("false")) multiplexer_1 (
    .in0(R1_output), .in1(R2_output), .in2(R3_output), .in3(R4_output), .in4(T1_output), .in5(T2_output),
    .in6(T3_output), .in7(T4_output), .out(OutA), .sel(OutASel));
  Multiplexer #(.select(3), .width(8), .enable("false")) multiplexer_2 (
    .in0(R1_output), .in1(R2_output), .in2(R3_output), .in3(R4_output), .in4(T1_output), .in5(T2_output),
    .in6(T3_output), .in7(T4_output), .out(OutB), .sel(OutBSel));
  Hex_Digit_Display hex_digit_display_5 (.value(OutA[7:4]), .dp(undriven_3));
  Hex_Digit_Display hex_digit_display_6 (.value(OutA[3:0]), .dp(undriven_5));
  Hex_Digit_Display hex_digit_display_7 (.value(OutB[7:4]), .dp(undriven_4));
  Hex_Digit_Display hex_digit_display_8 (.value(OutB[3:0]), .dp(undriven_6));
endmodule
