// Logisim project Part 2b.circ as structural Verilog: 1 circuit, main circuit main
module main (
  input  [2:0] RegSel,
  input  [1:0] OutCSel,
  input  CLK,
  input  [7:0] I,
  input  [1:0] FunSel,
  input  [1:0] OutDSel,
  output [7:0] OutC,
  output [7:0] OutD
);

  wire [2:0] not_1_out;
  wire [7:0] AR_output, PC_output, SP_output;

  Hex_Digit_Display hex_digit_display_1 (.value(I[3:0]));  // open: dp
  Hex_Digit_Display hex_digit_display_2 (.value(I[7:4]));  // open: dp
  assign not_1_out = ~RegSel;  // NOT_Gate not_1, 3 bits wide
  _8_bit_reg_main PC (.Input(I), .FunSel(FunSel), .Enable(not_1_out[2]), .CLK(CLK), .Output(PC_output));
  _8_bit_reg_main AR (.Input(I), .FunSel(FunSel), .Enable(not_1_out[1]), .CLK(CLK), .Output(AR_output));
  _8_bit_reg_main SP (.Input(I), .FunSel(FunSel), .Enable(not_1_out[0]), .CLK(CLK), .Output(SP_output));
  Multiplexer #(.select(2), .width(8), .enable("false")) multiplexer_1 (
    .in0(PC_output), .in1(PC_output), .in2(AR_output), .in3(SP_output), .out(OutC), .sel(OutCSel));
  Multiplexer #(.select(2), .width(8), .enable("false")) multiplexer_2 (
    .in0(PC_output), .in1(PC_output), .in2(AR_output), .in3(SP_output), .out(OutD), .sel(OutDSel));
  Hex_Digit_Display hex_digit_display_3 (.value(OutC[7:4]));  // open: dp
  Hex_Digit_Display hex_digit_display_4 (.value(OutC[3:0]));  // open: dp
  Hex_Digit_Display hex_digit_display_5 (.value(OutD[3:0]));  // open: dp
  Hex_Digit_Display hex_digit_display_6 (.value(OutD[7:4]));  // open: dp
endmodule
