// Logisim project part1.circ as structural Verilog: 3 circuits, main circuit 8-bit Dflipflop
module _8_bit_Dflipflop (
  input  CLK,
  input  [7:0] Input,
  input  Enable,
  output [7:0] Output
);

  D_Flip_Flop d_ff_1 (.clk(CLK), .D(Input[0]), .Q(Output[0]), .en(Enable));  // open: Qn, preset, reset
  D_Flip_Flop d_ff_2 (.clk(CLK), .D(Input[1]), .Q(Output[1]), .en(Enable));  // open: Qn, preset, reset
  D_Flip_Flop d_ff_3 (.clk(CLK), .D(Input[2]), .Q(Output[2]), .en(Enable));  // open: Qn, preset, reset
  D_Flip_Flop d_ff_4 (.clk(CLK), .D(Input[3]), .Q(Output[3]), .en(Enable));  // open: Qn, preset, reset
  D_Flip_Flop d_ff_5 (.clk(CLK), .D(Input[4]), .Q(Output[4]), .en(Enable));  // open: Qn, preset, reset
  D_Flip_Flop d_ff_6 (.clk(CLK), .D(Input[5]), .Q(Output[5]), .en(Enable));  // open: Qn, preset, reset
  D_Flip_Flop d_ff_7 (.clk(CLK), .D(Input[6]), .Q(Output[6]), .en(Enable));  // open: Qn, preset, reset
  D_Flip_Flop d_ff_8 (.clk(CLK), .D(Input[7]), .Q(Output[7]), .en(Enable));  // open: Qn, preset, reset
endmodule

module _8_Bit_Register (
  input  [7:0] Input,
  input  [1:0] FunSel,
  input  Enable,
  input  CLK,
  output [7:0] Output
);

  wire [7:0] adder_1_out, multiplexer_1_out, subtractor_1_out;

  _8_bit_Dflipflop u_8_bit_dflipflop_1 (.Input(multiplexer_1_out), .Enable(Enable), .Output(Output), .CLK(CLK));
  Subtractor subtractor_1 (.a(Output), .b(8'h1), .out(subtractor_1_out));  // open: bin, bout
  Adder adder_1 (.a(Output), .b(8'h1), .out(adder_1_out));  // open: cin, cout
  Multiplexer #(.select(2), .width(8)) multiplexer_1 (
    .in0(subtractor_1_out), .in1(adder_1_out), .in2(Input), .in3({8{1'b0}}), .out(multiplexer_1_out),
    .sel(FunSel), .en(Enable));
endmodule

module _16_bit_Dflipflop (
  input  CLK,
  input  [15:0] Input,
  input  Enable,
  output [15:0] Output
);

  _8_bit_Dflipflop u_8_bit_dflipflop_1 (.Input(Input[7:0]), .Enable(Enable), .Output(Output[7:0]), .CLK(CLK));
  _8_bit_Dflipflop u_8_bit_dflipflop_2 (.Input(Input[15:8]), .Enable(Enable), .Output(Output[15:8]), .CLK(CLK));
endmodule
