// Logisim project part3.circ as structural Verilog: 5 circuits, main circuit main
module main (
  input  [7:0] A,
  input  [7:0] B,
  input  CarryIn,
  input  [3:0] FunSel,
  output [7:0] OutALU,
  output [3:0] OutFlag
);

  wire [3:0] arithmetic_unit_1_outflag, buffer_not_unit_1_outflag, logic_unit_1_outflag, shift_unit_1_outflag;
  wire [7:0] arithmetic_unit_1_outalu, buffer_not_unit_1_outalu, logic_unit_1_outalu, shift_unit_1_outalu;

  Hex_Digit_Display hex_digit_display_1 (.value(A[3:0]));  // open: dp
  Hex_Digit_Display hex_digit_display_2 (.value(A[7:4]));  // open: dp
  Hex_Digit_Display hex_digit_display_3 (.value(B[7:4]));  // open: dp
  Hex_Digit_Display hex_digit_display_4 (.value(B[3:0]));  // open: dp
  Buffer__Not_Unit buffer_not_unit_1 (
    .A(A), .B(B), .FunSel(FunSel[1:0]), .OutALU(buffer_not_unit_1_outalu), .OutFlag(buffer_not_unit_1_outflag));
  Arithmetic_Unit arithmetic_unit_1 (
    .A(A), .B(B), .FunSel(FunSel[1:0]), .CarryIn(CarryIn), .OutALU(arithmetic_unit_1_outalu),
    .OutFlag(arithmetic_unit_1_outflag));
  Logic_Unit logic_unit_1 (
    .A(A), .B(B), .FunSel(FunSel[1:0]), .OutALU(logic_unit_1_outalu), .OutFlag(logic_unit_1_outflag));
  Shift_Unit shift_unit_1 (
    .A(A), .CarryIn(CarryIn), .FunSel(FunSel[2:0]), .OutALU(shift_unit_1_outalu),
    .OutFlag(shift_unit_1_outflag));
  Multiplexer #(.select(4), .width(4)) multiplexer_1 (
    .in0(buffer_not_unit_1_outflag), .in1(buffer_not_unit_1_outflag), .in2(buffer_not_unit_1_outflag),
    .in3(buffer_not_unit_1_outflag), .in4(arithmetic_unit_1_outflag), .in5(arithmetic_unit_1_outflag),
    .in6(arithmetic_unit_1_outflag), .in7(logic_unit_1_outflag), .in8(logic_unit_1_outflag),
    .in9(logic_unit_1_outflag), .in10(shift_unit_1_outflag), .in11(shift_unit_1_outflag),
    .in12(shift_unit_1_outflag), .in13(shift_unit_1_outflag), .in14(shift_unit_1_outflag),
    .in15(shift_unit_1_outflag), .out(OutFlag), .sel(FunSel));  // open: en
  Hex_Digit_Display hex_digit_display_5 (.value(OutALU[7:4]));  // open: dp
  Multiplexer #(.select(4), .width(8)) multiplexer_2 (
    .in0(buffer_not_unit_1_outalu), .in1(buffer_not_unit_1_outalu), .in2(buffer_not_unit_1_outalu),
    .in3(buffer_not_unit_1_outalu), .in4(arithmetic_unit_1_outalu), .in5(arithmetic_unit_1_outalu),
    .in6(arithmetic_unit_1_outalu), .in7(logic_unit_1_outalu), .in8(logic_unit_1_outalu),
    .in9(logic_unit_1_outalu), .in10(shift_unit_1_outalu), .in11(shift_unit_1_outalu),
    .in12(shift_unit_1_outalu), .in13(shift_unit_1_outalu), .in14(shift_unit_1_outalu),
    .in15(shift_unit_1_outalu), .out(OutALU), .sel(FunSel));  // open: en
  Hex_Digit_Display hex_digit_display_6 (.value(OutALU[3:0]));  // open: dp
endmodule

module Buffer__Not_Unit (
  input  [7:0] A,
  input  [7:0] B,
  input  [1:0] FunSel,
  output [7:0] OutALU,
  output [3:0] OutFlag
);

  wire [7:0] not_1_out, not_2_out;

  Hex_Digit_Display hex_digit_display_1 (.value(A[7:4]));  // open: dp
  Hex_Digit_Display hex_digit_display_2 (.value(B[7:4]));  // open: dp
  Hex_Digit_Display hex_digit_display_3 (.value(A[3:0]));  // open: dp
  Hex_Digit_Display hex_digit_display_4 (.value(B[3:0]));  // open: dp
  assign not_1_out = ~A;  // NOT_Gate not_1, 8 bits wide
  assign not_2_out = ~B;  // NOT_Gate not_2, 8 bits wide
  Multiplexer #(.select(2), .width(8)) multiplexer_1 (
    .in0(A), .in1(B), .in2(not_1_out), .in3(not_2_out), .out(OutALU), .sel(FunSel));  // open: en
  Hex_Digit_Display hex_digit_display_5 (.value(OutALU[7:4]));  // open: dp
  Hex_Digit_Display hex_digit_display_6 (.value(OutALU[3:0]));  // open: dp
  nor nor_1 (OutFlag[3], OutALU[0], OutALU[1], OutALU[2], OutALU[3], OutALU[4], OutALU[5], OutALU[6], OutALU[7]);

  assign OutFlag[1] = OutALU[7];
endmodule

module Arithmetic_Unit (
  input  [7:0] A,
  input  [7:0] B,
  input  [1:0] FunSel,
  input  CarryIn,
  output [7:0] OutALU,
  output [3:0] OutFlag
);

  wire adder_1_cout, and_1_out, and_2_out, and_3_out, and_4_out, and_5_out, not_1_out, not_2_out, not_3_out,
       not_4_out, or_1_out, or_2_out, subtractor_1_bout;
  wire [7:0] adder_1_out, subtractor_1_out;

  and and_1 (and_1_out, FunSel[0], CarryIn);
  Hex_Digit_Display hex_digit_display_1 (.value(A[7:4]));  // open: dp
  Hex_Digit_Display hex_digit_display_2 (.value(A[3:0]));  // open: dp
  Hex_Digit_Display hex_digit_display_3 (.value(B[7:4]));  // open: dp
  Hex_Digit_Display hex_digit_display_4 (.value(B[3:0]));  // open: dp
  not not_1 (not_1_out, A[7]);
  not not_2 (not_2_out, B[7]);
  not not_3 (not_3_out, OutALU[7]);
  Adder adder_1 (.a(A), .b(B), .out(adder_1_out), .cin(and_1_out), .cout(adder_1_cout));
  Subtractor subtractor_1 (.a(A), .b(B), .out(subtractor_1_out), .bout(subtractor_1_bout));  // open: bin
  not not_4 (not_4_out, subtractor_1_bout);
  and and_2 (and_2_out, not_1_out, not_2_out, OutALU[7]);
  or or_1 (or_1_out, and_2_out, and_3_out);
  and and_3 (and_3_out, A[7], B[7], not_3_out);
  and and_4 (and_4_out, A[7], not_2_out, not_3_out);
  or or_2 (or_2_out, and_4_out, and_5_out);
  and and_5 (and_5_out, not_1_out, B[7], OutALU[7]);
  Multiplexer #(.select(2), .width(8)) multiplexer_1 (
    .in0(adder_1_out), .in1(adder_1_out), .in2(subtractor_1_out), .out(OutALU), .sel(FunSel));  // open: in3, en
  Multiplexer #(.select(2)) multiplexer_2 (
    .in0(adder_1_cout), .in1(adder_1_cout), .in2(not_4_out), .out(OutFlag[2]), .sel(FunSel));  // open: in3, en
  Multiplexer #(.select(2)) multiplexer_3 (
    .in0(or_1_out), .in1(or_1_out), .in2(or_2_out), .out(OutFlag[0]), .sel(FunSel));  // open: in3, en
  Hex_Digit_Display hex_digit_display_5 (.value(OutALU[7:4]));  // open: dp
  Hex_Digit_Display hex_digit_display_6 (.value(OutALU[3:0]));  // open: dp
  nor nor_1 (OutFlag[3], OutALU[0], OutALU[1], OutALU[2], OutALU[3], OutALU[4], OutALU[5], OutALU[6], OutALU[7]);

  assign OutFlag[1] = OutALU[7];
endmodule

module Logic_Unit (
  input  [7:0] A,
  input  [7:0] B,
  input  [1:0] FunSel,
  output [7:0] OutALU,
  output [3:0] OutFlag
);

  wire [7:0] and_1_out, or_1_out, xor_1_out;

  Hex_Digit_Display hex_digit_display_1 (.value(A[7:4]));  // open: dp
  Hex_Digit_Display hex_digit_display_2 (.value(B[7:4]));  // open: dp
  Hex_Digit_Display hex_digit_display_3 (.value(A[3:0]));  // open: dp
  Hex_Digit_Display hex_digit_display_4 (.value(B[3:0]));  // open: dp
  assign or_1_out = A | B;  // OR_Gate or_1, 8 bits wide
  assign xor_1_out = A ^ B;  // XOR_Gate xor_1, 8 bits wide
  assign and_1_out = A & B;  // AND_Gate and_1, 8 bits wide
  Multiplexer #(.select(2), .width(8)) multiplexer_1 (
    .in0(or_1_out), .in1(xor_1_out), .in3(and_1_out), .out(OutALU), .sel(FunSel));  // open: in2, en
  Hex_Digit_Display hex_digit_display_5 (.value(OutALU[7:4]));  // open: dp
  Hex_Digit_Display hex_digit_display_6 (.value(OutALU[3:0]));  // open: dp
  nor nor_1 (OutFlag[3], OutALU[0], OutALU[1], OutALU[2], OutALU[3], OutALU[4], OutALU[5], OutALU[6], OutALU[7]);

  assign OutFlag[1] = OutALU[7];
endmodule

module Shift_Unit (
  input  [7:0] A,
  input  CarryIn,
  input  [2:0] FunSel,
  output [7:0] OutALU,
  output [3:0] OutFlag
);

  wire or_1_out, xor_1_out, xor_2_out;
  wire [7:0] shifter_1_out, shifter_2_out, shifter_3_out, shifter_4_out;

  Hex_Digit_Display hex_digit_display_1 (.value(A[3:0]));  // open: dp
  Hex_Digit_Display hex_digit_display_2 (.value(A[7:4]));  // open: dp
  Shifter shifter_1 (.in(A), .\dist (3'b001), .out(shifter_1_out));
  Shifter #(.shift("lr")) shifter_2 (.in(A), .\dist (3'b001), .out(shifter_2_out));
  Shifter shifter_3 (.in(A), .\dist (3'b001), .out(shifter_3_out));
  Shifter #(.shift("ar")) shifter_4 (.in(A), .\dist (3'b001), .out(shifter_4_out));
  xor xor_1 (xor_1_out, A[6], A[7]);
  xor xor_2 (xor_2_out, A[7], CarryIn);
  Multiplexer #(.select(3)) multiplexer_1 (
    .in2(A[7]), .in3(A[0]), .in6(A[7]), .in7(A[0]), .out(OutFlag[2]), .sel(FunSel));  // open: in0, in1, in4, in5, en
  Multiplexer #(.select(3)) multiplexer_2 (
    .in4(xor_1_out), .in6(xor_1_out), .in7(xor_2_out), .out(OutFlag[0]), .sel(FunSel));  // open: in0, in1, in2, in3, in5, en
  Multiplexer #(.select(3), .width(8)) multiplexer_3 (
    .in2(shifter_1_out), .in3(shifter_2_out), .in4(shifter_3_out), .in5(shifter_4_out),
    .in6({A[6:0], CarryIn}), .in7({CarryIn, A[7:1]}), .out(OutALU), .sel(FunSel));  // open: in0, in1, en
  Hex_Digit_Display hex_digit_display_3 (.value(OutALU[7:4]));  // open: dp
  or or_1 (or_1_out, ~FunSel[0], FunSel[1], ~FunSel[2]);  // OR_Gate
  Hex_Digit_Display hex_digit_display_4 (.value(OutALU[3:0]));  // open: dp
  nor nor_1 (OutFlag[3], OutALU[0], OutALU[1], OutALU[2], OutALU[3], OutALU[4], OutALU[5], OutALU[6], OutALU[7]);
  assign OutFlag[1] = or_1_out ? OutALU[7] : 1'bz;  // Controlled_Buffer controlled_buffer_1
endmodule
