// Logisim project part4.circ as structural Verilog: 1 circuit, main circuit main
module main (
  input  [3:0] RegSel,
  input  [1:0] FunSel,
  input  [3:0] TmpSel,
  input  [3:0] FunSel_2,
  input  [2:0] OutBSel,
  input  [2:0] OutASel,
  input  [1:0] MuxASel,
  input  [1:0] FunSel_3,
  input  [1:0] MuxBSel,
  input  [1:0] OutDSel,
  input  [1:0] OutCSel,
  input  in_12,
  input  in_13,
  input  in_14,
  input  in_15,
  input  [2:0] RegSel_2,
  input  L_H,
  input  [1:0] FunSel_4,
  output O,
  output N,
  output C,
  output Z
);

  wire CLK_out;
  wire [3:0] main_3_outflag;
  wire [7:0] IR_out_6, main_1_outa, main_1_outb, main_2_outc, main_2_outd, main_3_outalu, multiplexer_1_out,
       multiplexer_2_out, ram_1_data;
  wire [15:8] IR_out_6_2;

  Multiplexer #(.select(2), .width(8), .enable("false")) multiplexer_1 (
    .in0(main_3_outalu), .in1(ram_1_data), .in2(IR_out_6), .in3(main_2_outc), .out(multiplexer_1_out),
    .sel(MuxASel));
  Clock CLK (.out(CLK_out));
  Part_2a_main main_1 (
    .RegSel(RegSel), .FunSel(FunSel), .CLK(CLK_out), .TmpSel(TmpSel), .OutA(main_1_outa), .OutB(main_1_outb),
    .I(multiplexer_1_out), .OutASel(OutASel), .OutBSel(OutBSel));
  part1b_main IR (
    .out_6({IR_out_6_2, IR_out_6}), .L_H(L_H), .I(ram_1_data), .FunSel(FunSel_4), .CLK(CLK_out));  // open: EN
  Multiplexer #(.select(2), .width(8), .enable("false")) multiplexer_2 (
    .in0(main_3_outalu), .in1(ram_1_data), .in2(IR_out_6), .in3(main_2_outc), .out(multiplexer_2_out),
    .sel(MuxBSel));
  Part_2b_main main_2 (
    .I(multiplexer_2_out), .OutC(main_2_outc), .OutD(main_2_outd), .CLK(CLK_out), .RegSel(RegSel_2),
    .OutCSel(OutCSel), .OutDSel(OutDSel), .FunSel(FunSel_3));
  part3_main main_3 (
    .A(main_1_outa), .B(main_1_outb), .CarryIn(C), .FunSel(FunSel_2), .OutALU(main_3_outalu),
    .OutFlag(main_3_outflag));
  D_Flip_Flop d_ff_1 (.clk(CLK_out), .D(main_3_outflag[0]), .Q(O));  // open: Qn, preset, en, reset
  D_Flip_Flop d_ff_2 (.clk(CLK_out), .D(main_3_outflag[1]), .Q(N));  // open: Qn, preset, en, reset
  D_Flip_Flop d_ff_3 (.clk(CLK_out), .D(main_3_outflag[2]), .Q(C));  // open: Qn, preset, en, reset
  D_Flip_Flop d_ff_4 (.clk(CLK_out), .D(main_3_outflag[3]), .Q(Z));  // open: Qn, preset, en, reset
  RAM #(.bus("separate")) ram_1 (
    .addr(main_2_outd), .din(main_3_outalu), .data(ram_1_data), .str(in_12), .sel(in_13), .clk(CLK_out),
    .ld(in_14), .clr(in_15));

  // Notes on the sheet:
  //   Address
endmodule
