// Logisim project 16 bit d flip flop.circ as structural Verilog: 1 circuit, main circuit main
module main (
  input  CLK,
  input  EN,
  input  CLR,
  input  [15:0] A,
  output [15:0] Q
);

  D_Flip_Flop d_ff_1 (.clk(CLK), .D(A[0]), .Q(Q[0]), .en(EN), .reset(CLR));  // open: Qn, preset
  D_Flip_Flop d_ff_2 (.clk(CLK), .D(A[1]), .Q(Q[1]), .en(EN), .reset(CLR));  // open: Qn, preset
  D_Flip_Flop d_ff_3 (.clk(CLK), .D(A[2]), .Q(Q[2]), .en(EN), .reset(CLR));  // open: Qn, preset
  D_Flip_Flop d_ff_4 (.clk(CLK), .D(A[3]), .Q(Q[3]), .en(EN), .reset(CLR));  // open: Qn, preset
  D_Flip_Flop d_ff_5 (.clk(CLK), .D(A[4]), .Q(Q[4]), .en(EN), .reset(CLR));  // open: Qn, preset
  D_Flip_Flop d_ff_6 (.clk(CLK), .D(A[5]), .Q(Q[5]), .en(EN), .reset(CLR));  // open: Qn, preset
  D_Flip_Flop d_ff_7 (.clk(CLK), .D(A[6]), .Q(Q[6]), .en(EN), .reset(CLR));  // open: Qn, preset
  D_Flip_Flop d_ff_8 (.clk(CLK), .D(A[7]), .Q(Q[7]), .en(EN), .reset(CLR));  // open: Qn, preset
  D_Flip_Flop d_ff_9 (.clk(CLK), .D(A[8]), .Q(Q[8]), .en(EN), .reset(CLR));  // open: Qn, preset
  D_Flip_Flop d_ff_10 (.clk(CLK), .D(A[9]), .Q(Q[9]), .en(EN), .reset(CLR));  // open: Qn, preset
  D_Flip_Flop d_ff_11 (.clk(CLK), .D(A[10]), .Q(Q[10]), .en(EN), .reset(CLR));  // open: Qn, preset
  D_Flip_Flop d_ff_12 (.clk(CLK), .D(A[11]), .Q(Q[11]), .en(EN), .reset(CLR));  // open: Qn, preset
  D_Flip_Flop d_ff_13 (.clk(CLK), .D(A[12]), .Q(Q[12]), .en(EN), .reset(CLR));  // open: Qn, preset
  D_Flip_Flop d_ff_14 (.clk(CLK), .D(A[13]), .Q(Q[13]), .en(EN), .reset(CLR));  // open: Qn, preset
  D_Flip_Flop d_ff_15 (.clk(CLK), .D(A[14]), .Q(Q[14]), .en(EN), .reset(CLR));  // open: Qn, preset
  D_Flip_Flop d_ff_16 (.clk(CLK), .D(A[15]), .Q(Q[15]), .en(EN), .reset(CLR));  // open: Qn, preset
endmodule
