// Logisim project 16_bit_register_for_part_1b.circ as structural Verilog: 1 circuit, main circuit main
module main (
  input  [7:0] Input__0_7,
  input  [7:0] Input__8_15,
  input  CLK,
  input  EN,
  input  L_H,
  input  [1:0] FunSel,
  output [15:0] Q
);

  wire and_1_out, not_1_out;
  wire [7:0] D_Flip_Flop__0_7_q, D_Flip_Flop__8_15_q, multiplexer_1_out, multiplexer_2_out;
  wire [15:0] adder_1_out, multiplexer_3_out, subtractor_1_out;

  not not_1 (not_1_out, L_H);
  _8_bit_d_flip_flop_main D_Flip_Flop__0_7 (
    .CLK(CLK), .EN(not_1_out), .CLR(and_1_out), .D(Input__0_7), .Q(D_Flip_Flop__0_7_q));
  Multiplexer #(.width(8)) multiplexer_1 (
    .in0(Input__0_7), .in1(D_Flip_Flop__0_7_q), .out(multiplexer_1_out), .sel(L_H), .en(EN));
  and and_1 (and_1_out, FunSel[0], FunSel[1]);
  Multiplexer #(.width(8)) multiplexer_2 (
    .in0(D_Flip_Flop__8_15_q), .in1(Input__8_15), .out(multiplexer_2_out), .sel(L_H), .en(EN));
  Subtractor #(.width(16)) subtractor_1 (.a(Q), .b(16'h1), .out(subtractor_1_out));  // open: bin, bout
  _16_bit_d_flip_flop_main D_Flip_Flop (.CLK(CLK), .EN(EN), .A(multiplexer_3_out), .Q(Q));  // open: CLR
  _8_bit_d_flip_flop_main D_Flip_Flop__8_15 (
    .CLK(CLK), .EN(L_H), .CLR(and_1_out), .D(Input__8_15), .Q(D_Flip_Flop__8_15_q));
  Adder #(.width(16)) adder_1 (.a(Q), .b(16'h1), .out(adder_1_out));  // open: cin, cout
  Multiplexer #(.select(2), .width(16)) multiplexer_3 (
    .in0(subtractor_1_out), .in1(adder_1_out), .in2({multiplexer_1_out, multiplexer_2_out}),
    .in3({16{1'b0}}), .out(multiplexer_3_out), .sel(FunSel), .en(EN));
endmodule
