// Logisim project 8-bit-d-flipflop.circ as structural Verilog: 1 circuit, main circuit main
module main (
  input  CLK,
  input  [7:0] Input,
  input  Enable,
  output [7:0] Output
);

  D_Flip_Flop d_ff_1 (.clk(CLK), .D(Input[0]), .Q(Output[0]), .en(Enable));  // open: Qn, preset, reset
  D_Flip_Flop d_ff_2 (.clk(CLK), .D(Input[1]), .Q(Output[1]), .en(Enable));  // open: Qn, preset, reset
  D_Flip_Flop d_ff_3 (.clk(CLK), .D(Input[2]), .Q(Output[2]), .en(Enable));  // open: Qn, preset, reset
  D_Flip_Flop d_ff_4 (.clk(CLK), .D(Input[3]), .Q(Output[3]), .en(Enable));  // open: Qn, preset, reset
  D_Flip_Flop d_ff_5 (.clk(CLK), .D(Input[4]), .Q(Output[4]), .en(Enable));  // open: Qn, preset, reset
  D_Flip_Flop d_ff_6 (.clk(CLK), .D(Input[5]), .Q(Output[5]), .en(Enable));  // open: Qn, preset, reset
  D_Flip_Flop d_ff_7 (.clk(CLK), .D(Input[6]), .Q(Output[6]), .en(Enable));  // open: Qn, preset, reset
  D_Flip_Flop d_ff_8 (.clk(CLK), .D(Input[7]), .Q(Output[7]), .en(Enable));  // open: Qn, preset, reset
endmodule
