// Logisim project 8-bit-reg.circ as structural Verilog: 1 circuit, main circuit main
module main (
  input  [7:0] Input,
  input  [1:0] FunSel,
  input  Enable,
  input  CLK,
  output [7:0] Output
);

  wire [7:0] adder_1_out, multiplexer_1_out, subtractor_1_out;

  _8_bit_d_flipflop_main main_1 (.CLK(CLK), .Input(multiplexer_1_out), .Enable(Enable), .Output(Output));
  Subtractor subtractor_1 (.a(Output), .b(8'h1), .out(subtractor_1_out));  // open: bin, bout
  Adder adder_1 (.a(Output), .b(8'h1), .out(adder_1_out));  // open: cin, cout
  Multiplexer #(.select(2), .width(8)) multiplexer_1 (
    .in0(subtractor_1_out), .in1(adder_1_out), .in2(Input), .in3({8{1'b0}}), .out(multiplexer_1_out),
    .sel(FunSel), .en(Enable));
endmodule
