// Logisim project main.circ as structural Verilog: 2 circuits, main circuit main
module main (
  input  in_1
);

  wire CLK, d_ff_3_q, EnableP1B, L_H_P1B, ld, sl, st, Z;
  wire [1:0] FunSelP1B, FunSelP2A, FunSelP2B, MuxASel, MuxBSel, OutCSelP2B, OutDSelP2B;
  wire [2:0] OutASelP2A, OutBSelP2A, RegSelP2B;
  wire [3:0] FunSelP3, main_3_outflag, RegSelP2A, TmpSelP2A;
  wire [7:0] main_1_outa, main_1_outb, main_2_outc, main_2_outd, main_3_outalu, multiplexer_1_out,
       multiplexer_2_out, ram_1_data;
  wire [15:0] IR;

  Multiplexer #(.select(2), .width(8), .enable("false")) multiplexer_1 (
    .in0(main_3_outalu), .in1(ram_1_data), .in2(IR[7:0]), .in3(main_2_outc), .out(multiplexer_1_out),
    .sel(MuxASel));
  Clock u_CLK (.out(CLK));
  part1b_main u_IR (.out_6(IR), .L_H(L_H_P1B), .I(ram_1_data), .FunSel(FunSelP1B), .CLK(CLK), .EN(EnableP1B));
  Part_2a_main main_1 (
    .RegSel(RegSelP2A), .FunSel(FunSelP2A), .CLK(CLK), .TmpSel(TmpSelP2A), .OutA(main_1_outa),
    .OutB(main_1_outb), .I(multiplexer_1_out), .OutASel(OutASelP2A), .OutBSel(OutBSelP2A));
  Multiplexer #(.select(2), .width(8), .enable("false")) multiplexer_2 (
    .in0(main_3_outalu), .in1(ram_1_data), .in2(IR[7:0]), .in3(main_2_outc), .out(multiplexer_2_out),
    .sel(MuxBSel));
  Part_2b_main main_2 (
    .I(multiplexer_2_out), .OutC(main_2_outc), .OutD(main_2_outd), .CLK(CLK), .RegSel(RegSelP2B),
    .OutCSel(OutCSelP2B), .OutDSel(OutDSelP2B), .FunSel(FunSelP2B));
  part3_main main_3 (
    .A(main_1_outa), .B(main_1_outb), .CarryIn(d_ff_3_q), .FunSel(FunSelP3), .OutALU(main_3_outalu),
    .OutFlag(main_3_outflag));
  D_Flip_Flop d_ff_1 (.clk(CLK), .D(main_3_outflag[0]));  // open: Q, Qn, preset, en, reset
  D_Flip_Flop d_ff_2 (.clk(CLK), .D(main_3_outflag[1]));  // open: Q, Qn, preset, en, reset
  D_Flip_Flop d_ff_3 (.clk(CLK), .D(main_3_outflag[2]), .Q(d_ff_3_q));  // open: Qn, preset, en, reset
  D_Flip_Flop d_ff_4 (.clk(CLK), .D(main_3_outflag[3]), .Q(Z));  // open: Qn, preset, en, reset
  RAM #(.bus("separate")) ram_1 (
    .addr(main_2_outd), .din(main_3_outalu), .data(ram_1_data), .str(st), .sel(sl), .clk(CLK), .ld(ld),
    .clr(in_1));
  Control_Unit CONTROL_UNIT (
    .EnableP1B(EnableP1B), .IR(IR), .CLK(CLK), .L_HP1B(L_H_P1B), .FunSelP1B(FunSelP1B),
    .OutCSelP2B(OutCSelP2B), .RegSelP2B(RegSelP2B), .MuxASel(MuxASel), .MuxBSel(MuxBSel),
    .OutDSelP2B(OutDSelP2B), .FunSelP2B(FunSelP2B), .LD(ld), .SL(sl), .RegSelP2A(RegSelP2A),
    .FunSelP2A(FunSelP2A), .TmpSelP2A(TmpSelP2A), .OutBSelP2A(OutBSelP2A), .OutASelP2A(OutASelP2A), .Z(Z),
    .FunSelP3(FunSelP3), .st(st));

  // Notes on the sheet:
  //   Address
  //   O
  //   N
  //   C
  //   Z
endmodule

module Control_Unit (
  input  Z,
  input  CLK,
  input  [15:0] IR,
  output [1:0] FunSelP2A,
  output [1:0] FunSelP1B,
  output [1:0] MuxASel,
  output [2:0] RegSelP2B,
  output EnableP1B,
  output L_HP1B,
  output [1:0] MuxBSel,
  output [2:0] OutASelP2A,
  output SL,
  output [1:0] OutCSelP2B,
  output LD,
  output [3:0] FunSelP3,
  output st,
  output [2:0] OutBSelP2A,
  output [1:0] OutDSelP2B,
  output [3:0] RegSelP2A,
  output [1:0] FunSelP2B,
  output [3:0] TmpSelP2A
);

  wire and_1_out, and_2_out, and_3_out, and_4_out, and_5_out, and_6_out, and_7_out, and_8_out, and_10_out,
       and_11_out, and_12_out, and_13_out, and_14_out, and_15_out, and_16_out, and_17_out, and_18_out,
       and_19_out, and_20_out, and_21_out, and_22_out, and_23_out, and_24_out, and_25_out, and_26_out,
       and_27_out, and_28_out, and_29_out, and_30_out, and_31_out, and_32_out, and_33_out, and_34_out,
       and_35_out, and_36_out, and_37_out, and_38_out, and_39_out, and_40_out, and_41_out, and_42_out,
       and_43_out, and_44_out, and_45_out, and_46_out, and_47_out, and_48_out, and_49_out, and_50_out,
       and_51_out, and_52_out, and_53_out, and_54_out, and_55_out, and_56_out, and_57_out, and_58_out,
       and_59_out, and_60_out, and_61_out, and_62_out, and_63_out, and_64_out, and_65_out, and_66_out,
       and_67_out, and_68_out, and_69_out, and_70_out, and_71_out, and_72_out, and_73_out, and_74_out,
       and_75_out, and_76_out, and_77_out, and_78_out, and_79_out, and_80_out, and_81_out, and_82_out,
       and_83_out, and_84_out, and_85_out, and_86_out, and_87_out, and_88_out, and_89_out, and_90_out,
       and_91_out, Clear, Comb1, Comb2, Comb3, Comb4, D0, D1, D2, D3, D4, D5, D6, D7, D8, D9, D10, D11, D12,
       D13, D14, D15, d_ff_1_q, decoder_3_out0, decoder_3_out1, decoder_3_out2, decoder_3_out3,
       decoder_6_out0, decoder_6_out1, decoder_6_out2, decoder_6_out3, not_6_out, not_7_out, not_8_out,
       or_2_out, or_3_out, or_4_out, or_5_out, or_6_out, or_12_out, or_14_out, or_16_out, or_17_out,
       or_18_out, or_19_out, or_20_out, or_21_out, or_22_out, or_23_out, or_24_out, or_25_out, or_26_out,
       or_27_out, or_28_out, or_29_out, or_30_out, or_31_out, or_32_out, or_33_out, or_34_out, or_35_out,
       or_36_out, or_37_out, or_38_out, or_39_out, or_40_out, or_41_out, or_42_out, or_43_out, or_44_out,
       or_45_out, or_46_out, or_47_out, or_48_out, or_49_out, or_50_out, T0, T1, T2, T3, T4, T5, T6, T7;
  wire [2:0] controlled_buffer_44_out, counter_1_q;
  wire [2:2] not_1_out, not_3_out, not_4_out;
  wire [3:0] controlled_buffer_5_out, decoder_4_out3, decoder_5_out3, not_2_out, not_5_out;

  Counter #(.width(3), .max('h7)) counter_1 (
    .count(1'b1), .Q(counter_1_q), .clk(CLK), .clr(d_ff_1_q));  // open: load, D, carry
  D_Flip_Flop d_ff_1 (.clk(CLK), .D(Clear), .Q(d_ff_1_q), .en(1'b1), .reset(d_ff_1_q));  // open: Qn, preset
  Decoder #(.select(4), .enable("false")) decoder_1 (
    .out0(D0), .out1(D1), .out2(D2), .out3(D3), .out4(D4), .out5(D5), .out6(D6), .out7(D7), .out8(D8),
    .out9(D9), .out10(D10), .out11(D11), .out12(D12), .out13(D13), .out14(D14), .out15(D15), .sel(IR[15:12]));
  Decoder #(.select(3), .enable("false")) decoder_2 (
    .out0(T0), .out1(T1), .out2(T2), .out3(T3), .out4(T4), .out5(T5), .out6(T6), .out7(T7), .sel(counter_1_q));
  or or_1 (st, and_6_out, and_12_out);
  assign Clear = or_5_out ? 1'b1 : 1'bz;  // Controlled_Buffer controlled_buffer_1
  and and_1 (and_1_out, T4, Comb2);
  assign FunSelP1B = or_2_out ? 2'b10 : 2'bz;  // Controlled_Buffer controlled_buffer_2
  or or_2 (or_2_out, T1, T0);
  or or_3 (or_3_out, ~T0, T1);  // OR_Gate
  and and_2 (and_2_out, D11, T2);
  or or_4 (or_4_out, and_2_out, and_3_out);
  and and_3 (and_3_out, D12, T3);
  and and_4 (and_4_out, D1, ~IR[10]);  // AND_Gate
  and and_5 (and_5_out, T3, D12);
  and and_6 (and_6_out, T2, D2);
  or or_5 (or_5_out, and_1_out, and_8_out, and_7_out);
  and and_7 (and_7_out, T2, or_14_out);
  and and_8 (and_8_out, T3, or_6_out);
  or or_6 (or_6_out, Comb1, Comb4, D12, D11);
  or or_7 (Comb1, D6, D9, D10);
  or or_8 (Comb2, D4, D5, D7, D8);
  or or_9 (Comb3, D3, D13, D14);
  or or_10 (Comb4, D13, D14);
  or or_11 (EnableP1B, T0, T1);
  and and_9 (L_HP1B, or_3_out, EnableP1B);
  and and_10 (and_10_out, T2, or_12_out);
  or or_12 (or_12_out, and_4_out, D2);
  or or_13 (LD, T0, T1, and_5_out, and_11_out);
  and and_11 (and_11_out, D1, ~IR[10], T2);  // AND_Gate
  and and_12 (and_12_out, T2, D11);
  or or_14 (or_14_out, D15, D0, D2, D3, D1);
  or or_15 (SL, T0, T1, or_4_out, and_10_out);
  and and_13 (and_13_out, or_16_out, T3);
  or or_16 (or_16_out, D2, D3);
  and and_14 (and_14_out, D12, T3);
  and and_15 (and_15_out, T2, or_17_out);
  or or_17 (or_17_out, Comb1, Comb2, and_16_out, and_17_out);
  and and_16 (and_16_out, D1, IR[10]);
  and and_17 (and_17_out, Comb3, IR[10]);
  and and_18 (and_18_out, D1, ~IR[10], T2);  // AND_Gate
  not not_1 (not_1_out[2], IR[6]);
  assign RegSelP2A = and_13_out ? 4'b1111 : 4'bz;  // Controlled_Buffer controlled_buffer_3
  or or_18 (or_18_out, and_35_out, and_27_out, and_28_out, and_36_out, and_37_out, and_19_out);
  assign RegSelP2A = or_18_out ? controlled_buffer_5_out : 4'bz;  // Controlled_Buffer controlled_buffer_4
  and and_19 (and_19_out, D1, T2, IR[10]);
  assign controlled_buffer_5_out = decoder_3_out0 ? 4'b0111 : 4'bz;  // Controlled_Buffer controlled_buffer_5
  assign controlled_buffer_5_out = decoder_3_out1 ? 4'b1011 : 4'bz;  // Controlled_Buffer controlled_buffer_6
  assign controlled_buffer_5_out = decoder_3_out2 ? 4'b1101 : 4'bz;  // Controlled_Buffer controlled_buffer_7
  assign controlled_buffer_5_out = decoder_3_out3 ? 4'b1110 : 4'bz;  // Controlled_Buffer controlled_buffer_8
  assign TmpSelP2A = and_20_out ? not_5_out : 4'bz;  // Controlled_Buffer controlled_buffer_9
  and and_20 (and_20_out, or_21_out, T2);
  assign FunSelP2A = or_19_out ? 2'b10 : 2'bz;  // Controlled_Buffer controlled_buffer_10
  assign FunSelP2A = and_30_out ? 2'b01 : 2'bz;  // Controlled_Buffer controlled_buffer_11
  or or_19 (or_19_out, and_14_out, and_18_out, and_15_out, and_22_out);
  assign FunSelP2A = and_21_out ? 2'b00 : 2'bz;  // Controlled_Buffer controlled_buffer_12
  and and_21 (and_21_out, D14, T3, IR[10]);
  and and_22 (and_22_out, IR[10], or_22_out);
  assign OutASelP2A = or_20_out ? {1'b0, IR[9:8]} : 3'bz;  // Controlled_Buffer controlled_buffer_13
  and and_23 (and_23_out, Comb3, T2, IR[6]);
  or or_20 (or_20_out, and_33_out, and_34_out);
  assign OutASelP2A = and_23_out ? {1'b0, IR[5:4]} : 3'bz;  // Controlled_Buffer controlled_buffer_14
  assign OutASelP2A = and_24_out ? {not_1_out[2], IR[5:4]} : 3'bz;  // Controlled_Buffer controlled_buffer_15
  assign OutASelP2A = and_25_out ? {not_3_out[2], IR[1:0]} : 3'bz;  // Controlled_Buffer controlled_buffer_16
  and and_24 (and_24_out, Comb1, T3);
  and and_25 (and_25_out, Comb2, T4);
  assign OutBSelP2A = and_26_out ? {not_4_out[2], IR[5:4]} : 3'bz;  // Controlled_Buffer controlled_buffer_17
  and and_26 (and_26_out, Comb2, T4);
  and and_27 (and_27_out, Comb3, T2, IR[10]);
  and and_28 (and_28_out, ~IR[10], D1, T2);  // AND_Gate
  Decoder #(.select(2), .enable("false")) decoder_3 (
    .out0(decoder_3_out0), .out1(decoder_3_out1), .out2(decoder_3_out2), .out3(decoder_3_out3), .sel(IR[9:8]));
  or or_21 (or_21_out, Comb1, Comb2);
  assign TmpSelP2A = and_29_out ? not_2_out : 4'bz;  // Controlled_Buffer controlled_buffer_18
  assign not_2_out = ~decoder_4_out3;  // NOT_Gate not_2, 4 bits wide
  and and_29 (and_29_out, Comb2, T3);
  and and_30 (and_30_out, D13, T3, IR[10]);
  and and_31 (and_31_out, Comb2, T4);
  or or_22 (or_22_out, and_31_out, and_32_out);
  and and_32 (and_32_out, or_24_out, T3);
  and and_33 (and_33_out, D2, T2);
  and and_34 (and_34_out, D11, T2);
  not not_3 (not_3_out[2], IR[2]);
  not not_4 (not_4_out[2], IR[6]);
  or or_23 (or_23_out, and_38_out, and_39_out);
  and and_35 (and_35_out, or_23_out, IR[10]);
  and and_36 (and_36_out, IR[10], T3, Comb4);
  and and_37 (and_37_out, T3, D12);
  assign not_5_out = ~decoder_5_out3;  // NOT_Gate not_5, 4 bits wide
  Decoder #(.select(2), .enable("false")) decoder_4 (
    .out0(decoder_4_out3[3]), .out1(decoder_4_out3[2]), .out2(decoder_4_out3[1]), .out3(decoder_4_out3[0]),
    .sel(IR[1:0]));
  or or_24 (or_24_out, Comb1, Comb2);
  and and_38 (and_38_out, Comb1, T3);
  and and_39 (and_39_out, Comb2, T4);
  Decoder #(.select(2), .enable("false")) decoder_5 (
    .out0(decoder_5_out3[3]), .out1(decoder_5_out3[2]), .out2(decoder_5_out3[1]), .out3(decoder_5_out3[0]),
    .sel(IR[5:4]));
  and and_40 (and_40_out, D1, ~IR[10], T2);  // AND_Gate
  and and_41 (and_41_out, T3, D12);
  and and_42 (and_42_out, Comb3, T2, IR[6]);
  and and_43 (and_43_out, Comb2, T4);
  and and_44 (and_44_out, Comb1, T3);
  and and_45 (and_45_out, IR[6], Comb3, T2);
  and and_46 (and_46_out, Comb2, T4);
  and and_47 (and_47_out, Comb1, T3);
  and and_48 (and_48_out, D4, T4);
  and and_49 (and_49_out, D8, T4);
  and and_50 (and_50_out, D7, T4);
  assign MuxASel = or_25_out ? 2'b01 : 2'bz;  // Controlled_Buffer controlled_buffer_19
  assign MuxASel = or_28_out ? 2'b11 : 2'bz;  // Controlled_Buffer controlled_buffer_20
  or or_25 (or_25_out, and_40_out, and_41_out);
  assign MuxASel = or_26_out ? 2'b00 : 2'bz;  // Controlled_Buffer controlled_buffer_21
  or or_26 (or_26_out, and_42_out, and_43_out, and_44_out);
  assign MuxASel = and_56_out ? 2'b10 : 2'bz;  // Controlled_Buffer controlled_buffer_22
  assign MuxBSel = and_57_out ? 2'b11 : 2'bz;  // Controlled_Buffer controlled_buffer_23
  assign MuxBSel = or_27_out ? 2'b00 : 2'bz;  // Controlled_Buffer controlled_buffer_24
  or or_27 (or_27_out, and_45_out, and_46_out, and_47_out);
  assign MuxBSel = and_58_out ? 2'b10 : 2'bz;  // Controlled_Buffer controlled_buffer_25
  assign FunSelP3 = and_48_out ? 4'b0111 : 4'bz;  // Controlled_Buffer controlled_buffer_26
  assign FunSelP3 = and_59_out ? 4'b1000 : 4'bz;  // Controlled_Buffer controlled_buffer_27
  assign FunSelP3 = and_49_out ? 4'b0110 : 4'bz;  // Controlled_Buffer controlled_buffer_28
  assign FunSelP3 = and_60_out ? 4'b1010 : 4'bz;  // Controlled_Buffer controlled_buffer_29
  assign FunSelP3 = and_50_out ? 4'b0100 : 4'bz;  // Controlled_Buffer controlled_buffer_30
  assign FunSelP3 = and_61_out ? 4'b1011 : 4'bz;  // Controlled_Buffer controlled_buffer_31
  assign FunSelP3 = and_51_out ? 4'b0010 : 4'bz;  // Controlled_Buffer controlled_buffer_32
  and and_51 (and_51_out, D6, T3);
  and and_52 (and_52_out, IR[6], Comb3, T2);
  and and_53 (and_53_out, or_32_out, T2);
  and and_54 (and_54_out, Comb2, T3);
  or or_28 (or_28_out, and_53_out, and_54_out, and_55_out);
  and and_55 (and_55_out, Comb3, T2, ~IR[6]);  // AND_Gate
  and and_56 (and_56_out, T2, IR[10], D1);
  and and_57 (and_57_out, Comb3, ~IR[6], T2);  // AND_Gate
  and and_58 (and_58_out, T2, or_29_out);
  or or_29 (or_29_out, D0, and_63_out);
  and and_59 (and_59_out, D5, T4);
  and and_60 (and_60_out, D9, T3);
  and and_61 (and_61_out, D10, T3);
  assign FunSelP3 = or_30_out ? 4'b0000 : 4'bz;  // Controlled_Buffer controlled_buffer_33
  or or_30 (or_30_out, and_52_out, or_31_out);
  or or_31 (or_31_out, and_64_out, and_62_out);
  and and_62 (and_62_out, D11, T2);
  or or_32 (or_32_out, Comb2, Comb1);
  and and_63 (and_63_out, ~Z, D15);  // AND_Gate
  and and_64 (and_64_out, D2, T2);
  and and_65 (and_65_out, ~Z, D15);  // AND_Gate
  or or_33 (or_33_out, D11, D12);
  and and_66 (and_66_out, T3, ~IR[10], D13);  // AND_Gate
  and and_67 (and_67_out, T2, D12);
  and and_68 (and_68_out, T3, ~IR[10], D14);  // AND_Gate
  and and_69 (and_69_out, T3, D11);
  or or_34 (or_34_out, D0, and_65_out);
  and and_70 (and_70_out, or_34_out, T2);
  assign RegSelP2B = or_35_out ? 3'b110 : 3'bz;  // Controlled_Buffer controlled_buffer_34
  and and_71 (and_71_out, or_33_out, T2);
  or or_35 (or_35_out, and_71_out, and_72_out);
  and and_72 (and_72_out, D11, T3);
  and and_73 (and_73_out, D2, T2);
  and and_74 (and_74_out, D1, ~IR[10], T2);  // AND_Gate
  or or_36 (or_36_out, and_66_out, and_67_out);
  or or_37 (or_37_out, T1, or_36_out, T0);
  or or_38 (or_38_out, and_68_out, and_69_out);
  assign RegSelP2B = and_77_out ? 3'b111 : 3'bz;  // Controlled_Buffer controlled_buffer_35
  assign RegSelP2B = or_39_out ? 3'b011 : 3'bz;  // Controlled_Buffer controlled_buffer_36
  or or_39 (or_39_out, and_70_out, T1, T0);
  assign RegSelP2B = or_42_out ? controlled_buffer_44_out : 3'bz;  // Controlled_Buffer controlled_buffer_37
  and and_75 (and_75_out, T3, Comb4, not_8_out);
  assign OutCSelP2B = or_43_out ? IR[5:4] : 2'bz;  // Controlled_Buffer controlled_buffer_38
  assign OutCSelP2B = and_76_out ? IR[1:0] : 2'bz;  // Controlled_Buffer controlled_buffer_39
  and and_76 (and_76_out, Comb2, T3);
  assign OutDSelP2B = or_40_out ? 2'b10 : 2'bz;  // Controlled_Buffer controlled_buffer_40
  or or_40 (or_40_out, and_73_out, and_74_out);
  assign FunSelP2B = or_37_out ? 2'b01 : 2'bz;  // Controlled_Buffer controlled_buffer_41
  assign FunSelP2B = or_41_out ? 2'b10 : 2'bz;  // Controlled_Buffer controlled_buffer_42
  or or_41 (or_41_out, and_81_out, and_82_out, and_83_out);
  assign FunSelP2B = or_38_out ? 2'b00 : 2'bz;  // Controlled_Buffer controlled_buffer_43
  and and_77 (and_77_out, D2, T2);
  assign controlled_buffer_44_out = or_47_out ? 3'b011 : 3'bz;  // Controlled_Buffer controlled_buffer_44
  assign controlled_buffer_44_out = decoder_6_out2 ? 3'b101 : 3'bz;  // Controlled_Buffer controlled_buffer_45
  assign controlled_buffer_44_out = decoder_6_out3 ? 3'b110 : 3'bz;  // Controlled_Buffer controlled_buffer_46
  or or_42 (or_42_out, and_75_out, and_78_out, and_84_out);
  and and_78 (and_78_out, T2, not_8_out, Comb3);
  and and_79 (and_79_out, not_6_out, Comb3, T2);
  or or_43 (or_43_out, and_79_out, and_80_out);
  and and_80 (and_80_out, or_49_out, T2);
  assign OutDSelP2B = or_44_out ? 2'b00 : 2'bz;  // Controlled_Buffer controlled_buffer_47
  or or_44 (or_44_out, T1, T0);
  assign OutDSelP2B = or_45_out ? 2'b11 : 2'bz;  // Controlled_Buffer controlled_buffer_48
  or or_45 (or_45_out, and_85_out, and_86_out);
  and and_81 (and_81_out, or_50_out, T2);
  and and_82 (and_82_out, Comb3, T2, not_7_out);
  and and_83 (and_83_out, not_7_out, or_46_out);
  or or_46 (or_46_out, and_88_out, and_89_out);
  or or_47 (or_47_out, decoder_6_out0, decoder_6_out1);
  or or_48 (or_48_out, and_90_out, and_91_out);
  and and_84 (and_84_out, or_48_out, not_8_out);
  not not_6 (not_6_out, IR[6]);
  or or_49 (or_49_out, Comb1, Comb2);
  and and_85 (and_85_out, T2, D11);
  and and_86 (and_86_out, T3, D12);
  or or_50 (or_50_out, D0, and_87_out);
  and and_87 (and_87_out, ~Z, D15);  // AND_Gate
  not not_7 (not_7_out, IR[10]);
  and and_88 (and_88_out, Comb1, T3);
  and and_89 (and_89_out, Comb2, T4);
  Decoder #(.select(2), .enable("false")) decoder_6 (
    .out0(decoder_6_out0), .out1(decoder_6_out1), .out2(decoder_6_out2), .out3(decoder_6_out3), .sel(IR[9:8]));
  and and_90 (and_90_out, Comb1, T3);
  and and_91 (and_91_out, Comb2, T4);
  not not_8 (not_8_out, IR[10]);

  // Other names for the same wires on the sheet: ADDRESS[7:0] = IR[7:0]; IR_4 = IR[4]; SRCREG1[3:0] = IR[7:4];
  //   IR_5 = IR[5]; DESTREG[3:0] = IR[11:8]; IR_8 = IR[8]; RegSel[1:0] = IR[9:8]; IR_9 = IR[9];
  //   Addressing_Mode = IR[10]; IR_10 = IR[10]; IR_11 = IR[11]; IR_12 = IR[12]; OPCODE[3:0] = IR[15:12];
  //   IR_13 = IR[13]; IR_14 = IR[14]; IR_15 = IR[15]; IR_6 = IR[6]; IR_7 = IR[7]; IR_0 = IR[0];
  //   SRCREG2[3:0] = IR[3:0]; IR_1 = IR[1]; IR_2 = IR[2]; IR_3 = IR[3]

  // Notes on the sheet:
  //   Timing
  //   For All type of Instructions
  //   WITH address ref.
  //    WITHOUT address ref.
  //   Part1B
  //   Memory Selectors
  //   P2A
  //   MUXes
  //   ALU (P3)
  //   ARF (P2B)
endmodule
