// Logisim project part1b.circ as structural Verilog: 1 circuit, main circuit main
module main (
  input  L_H,
  input  [7:0] I,
  input  [1:0] FunSel,
  input  EN,
  input  CLK,
  output [15:0] out_6
);

  wire not_1_out;
  wire [7:0] demultiplexer_1_out0, demultiplexer_1_out1;

  Hex_Digit_Display hex_digit_display_1 (.value(I[7:4]));  // open: dp
  Hex_Digit_Display hex_digit_display_2 (.value(I[3:0]));  // open: dp
  not not_1 (not_1_out, L_H);
  Demultiplexer #(.width(8)) demultiplexer_1 (
    .out0(demultiplexer_1_out0), .out1(demultiplexer_1_out1), .in(I), .sel(not_1_out), .en(EN));
  _16_bit_register_for_part_1b_main main_1 (
    .Input__0_7(demultiplexer_1_out0), .Input__8_15(demultiplexer_1_out1), .L_H(not_1_out), .FunSel(FunSel),
    .CLK(CLK), .EN(EN), .Q(out_6));
  Hex_Digit_Display hex_digit_display_3 (.value(out_6[11:8]));  // open: dp
  Hex_Digit_Display hex_digit_display_4 (.value(out_6[15:12]));  // open: dp
  Hex_Digit_Display hex_digit_display_5 (.value(out_6[7:4]));  // open: dp
  Hex_Digit_Display hex_digit_display_6 (.value(out_6[3:0]));  // open: dp
endmodule
